# Fritzing sketch Sketch (saved by Fritzing 0.9.6b)
breadboards: 1

parts:
  U1 = NodeMCU V3.0
  DHT1 = DHT22 Humidity and Temperature Sensor
  R1 = Resistor [tolerance=±5% resistance=4.7k package="0402 [SMD]"]

nets:
  N1: U1.D3, R1.Pin_0
  3V3: U1.3V3, DHT1.VDD, DHT1.DATA, R1.Pin_1
  N2: U1.GND#6, U1.GND#13, U1.GND#16, U1.GND#33, DHT1.GND

custom parts:
  NodeMCU V3.0: ESP8266 based NodeMCU
